// Logisim project How_To_Design_A_CPU_3.circ as structural Verilog: 1 circuit, main circuit main
module main (
  input  A_0,
  input  A_0_2,
  input  B_0,
  input  in_4,
  input  B_0_2,
  input  in_6,
  input  C_in,
  input  A,
  input  [3:0] bus_A,
  input  is_addition,
  input  C_in_2,
  input  [3:0] bus_A_2,
  input  C_in_3,
  input  in_14,
  input  B,
  input  in_16,
  input  A_1,
  input  C_in_4,
  input  A_1_2,
  input  B_1,
  input  [3:0] bus_B,
  input  [3:0] bus_B_2,
  input  [3:0] bus_A_3,
  input  B_1_2,
  input  [3:0] bus_B_3,
  input  A_2,
  input  A_2_2,
  input  B_2,
  input  B_2_2,
  input  A_3,
  input  A_3_2,
  input  B_3,
  input  B_3_2,
  output S_0,
  output S_0_2,
  output out_36,
  output [3:0] out_37,
  output [3:0] bus_S,
  output S,
  output out_40,
  output out_41,
  output C_out,
  output [3:0] out_43,
  output S_1,
  output [3:0] Result,
  output S_1_2,
  output out_47,
  output S_2,
  output S_2_2,
  output S_3,
  output S_3_2,
  output C_out_2,
  output C_out_3,
  output C_out_4
);

  wire and_2_out, and_3_out, and_4_out, and_5_out, and_6_out, and_7_out, and_8_out, and_9_out, and_10_out,
       and_11_out, and_12_out, and_13_out, and_14_out, and_15_out, and_16_out, and_17_out, and_18_out,
       and_19_out, and_20_out, and_21_out, and_22_out, and_23_out, and_24_out, and_25_out, and_26_out,
       and_27_out, multiplexer_2_out, not_1_out, not_2_out, not_3_out, not_4_out, or_2_out, or_3_out,
       or_4_out, or_6_out, or_7_out, or_8_out, or_10_out, or_11_out, or_12_out, xor_2_out, xor_4_out,
       xor_6_out, xor_8_out, xor_10_out, xor_12_out, xor_13_out, xor_14_out, xor_15_out, xor_20_out,
       xor_21_out, xor_22_out, xor_23_out;
  wire [3:0] multiplexer_1_out, not_5_out, not_6_out;

  xor xor_1 (out_36, in_6, in_14);
  and and_1 (out_41, in_6, in_14);
  xor xor_2 (xor_2_out, A, B);
  xor xor_3 (S, xor_2_out, C_in_4);
  and and_2 (and_2_out, xor_2_out, C_in_4);
  and and_3 (and_3_out, A, B);
  or or_1 (C_out, and_2_out, and_3_out);
  xor xor_4 (xor_4_out, A_0, B_0);
  xor xor_5 (S_0, xor_4_out, C_in);
  and and_4 (and_4_out, xor_4_out, C_in);
  and and_5 (and_5_out, A_0, B_0);
  xor xor_6 (xor_6_out, A_1, B_1);
  xor xor_7 (S_1, xor_6_out, or_2_out);
  and and_6 (and_6_out, xor_6_out, or_2_out);
  and and_7 (and_7_out, A_1, B_1);
  xor xor_8 (xor_8_out, A_2, B_2);
  xor xor_9 (S_2, xor_8_out, or_3_out);
  and and_8 (and_8_out, xor_8_out, or_3_out);
  and and_9 (and_9_out, A_2, B_2);
  xor xor_10 (xor_10_out, A_3, B_3);
  xor xor_11 (S_3, xor_10_out, or_4_out);
  and and_10 (and_10_out, xor_10_out, or_4_out);
  and and_11 (and_11_out, A_3, B_3);
  or or_2 (or_2_out, and_4_out, and_5_out);
  or or_3 (or_3_out, and_6_out, and_7_out);
  or or_4 (or_4_out, and_8_out, and_9_out);
  or or_5 (C_out_2, and_10_out, and_11_out);
  not not_1 (not_1_out, B_0_2);
  not not_2 (not_2_out, B_1_2);
  not not_3 (not_3_out, B_2_2);
  not not_4 (not_4_out, B_3_2);
  xor xor_12 (xor_12_out, A_0_2, not_1_out);
  and and_12 (and_12_out, xor_12_out, C_in_2);
  and and_13 (and_13_out, A_0_2, not_1_out);
  xor xor_13 (xor_13_out, A_1_2, not_2_out);
  and and_14 (and_14_out, xor_13_out, or_6_out);
  and and_15 (and_15_out, A_1_2, not_2_out);
  xor xor_14 (xor_14_out, A_2_2, not_3_out);
  and and_16 (and_16_out, xor_14_out, or_7_out);
  and and_17 (and_17_out, A_2_2, not_3_out);
  xor xor_15 (xor_15_out, A_3_2, not_4_out);
  and and_18 (and_18_out, xor_15_out, or_8_out);
  and and_19 (and_19_out, A_3_2, not_4_out);
  xor xor_16 (S_0_2, xor_12_out, C_in_2);
  or or_6 (or_6_out, and_12_out, and_13_out);
  xor xor_17 (S_1_2, xor_13_out, or_6_out);
  or or_7 (or_7_out, and_14_out, and_15_out);
  xor xor_18 (S_2_2, xor_14_out, or_7_out);
  or or_8 (or_8_out, and_16_out, and_17_out);
  xor xor_19 (S_3_2, xor_15_out, or_8_out);
  or or_9 (C_out_3, and_18_out, and_19_out);
  assign not_5_out = ~bus_B;  // NOT_Gate not_5, 4 bits wide
  xor xor_20 (xor_20_out, bus_A_2[0], not_5_out[0]);
  xor xor_21 (xor_21_out, bus_A_2[1], not_5_out[1]);
  xor xor_22 (xor_22_out, bus_A_2[2], not_5_out[2]);
  xor xor_23 (xor_23_out, bus_A_2[3], not_5_out[3]);
  xor xor_24 (bus_S[0], xor_20_out, C_in_3);
  and and_20 (and_20_out, xor_20_out, C_in_3);
  or or_10 (or_10_out, and_20_out, and_21_out);
  and and_21 (and_21_out, bus_A_2[0], not_5_out[0]);
  xor xor_25 (bus_S[1], xor_21_out, or_10_out);
  and and_22 (and_22_out, xor_21_out, or_10_out);
  or or_11 (or_11_out, and_22_out, and_23_out);
  and and_23 (and_23_out, bus_A_2[1], not_5_out[1]);
  xor xor_26 (bus_S[2], xor_22_out, or_11_out);
  and and_24 (and_24_out, xor_22_out, or_11_out);
  or or_12 (or_12_out, and_24_out, and_25_out);
  and and_25 (and_25_out, bus_A_2[2], not_5_out[2]);
  xor xor_27 (bus_S[3], xor_23_out, or_12_out);
  and and_26 (and_26_out, xor_23_out, or_12_out);
  or or_13 (C_out_4, and_26_out, and_27_out);
  and and_27 (and_27_out, bus_A_2[3], not_5_out[3]);
  Adder #(.width(4)) adder_1 (.a(bus_A), .b(bus_B_2), .out(out_37), .cin(in_4), .cout(out_40));
  Subtractor #(.width(4)) subtractor_1 (.a(bus_A), .b(bus_B_2), .out(out_43), .bin(in_16), .bout(out_47));
  Multiplexer #(.width(4), .enable("false")) multiplexer_1 (
    .in0(bus_B_3), .in1(not_6_out), .out(multiplexer_1_out), .sel(is_addition));
  assign not_6_out = ~bus_B_3;  // NOT_Gate not_6, 4 bits wide
  Multiplexer #(.enable("false")) multiplexer_2 (.in0(1'b0), .in1(1'b1), .out(multiplexer_2_out), .sel(is_addition));
  Adder #(.width(4)) adder_2 (.a(bus_A_3), .b(multiplexer_1_out), .out(Result), .cin(multiplexer_2_out));  // open: cout
  // AND_Gate and_28 is placed but not wired

  // Notes on the sheet:
  //   Half Adder | 半加法器
  //   Full Adder | 全加法器
  //   4-bit Full Adder | 四位全加法器
  //   4-bit Substractor | 四位减法器
  //   4-bit Substractor Bus Ver, | 四位减法器 总线版
  //   Adder & Subtractor Modules | 加减法模块
  //   Adder & Subtractor Module | 加减法器
endmodule
